# Fritzing sketch 2.LCD_I2C (saved by Fritzing 0.9.3b)
breadboards: 1

parts:
  Raspberry_Pi_1 = Raspberry Pi 3 [part_number=RPI-3-V1.2]  # not connected
  Componente2 = Adafruit T-Cobbler Plus [part_number="Adafruit #1989 and #2028"]
  Componente1 = LCD1602-I2C

nets:
  N1: Componente2.SDA, Componente1.SDA
  N2: Componente2.SCL, Componente1.SCL
  GND: Componente2.GND, Componente1.GND
  +5V: Componente2.+5V, Componente1.VCC

custom parts:
  Adafruit T-Cobbler Plus: The Raspberry Pi has landed on the Maker World like a 40-GPIO pinned, quad-USB ported, credit card sized bomb of DIY joy. And while you can use most of our great Model B accessories by hooking up our downgrade cable, its probably a good time to upgrade your set up and accessorize using all of the 40 pins. That's why we now carry the Assembled Adafruit Pi T-Cobbler Plus - Breakout + Cable for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
  LCD1602-I2C: A standard character display, usually with 2x16 characters. Comes in many colors with LCM1602 IIC attached.
