# Fritzing sketch m.Motores (saved by Fritzing 0.9.3b)
breadboards: 1

parts:
  Raspberry_Pi_1 = Raspberry Pi 3 [part_number=RPI-3-V1.2]  # not connected
  Componente2 = Adafruit T-Cobbler Plus [part_number="Adafruit #1989 and #2028"]
  S1 = H-Bridge with L298N
  VCC1 = 4 x AAA Battery Mount
  M1 = DC Motor
  M2 = DC Motor

nets:
  GND: Componente2.GND, S1.GND, VCC1.-
  N1: Componente2.MISO, S1.IN4
  N2: Componente2.SCLK, S1.IN3
  N3: Componente2.CE0, S1.IN1
  N4: Componente2.CE1, S1.IN2
  N5: S1.12V, VCC1.+
  N6: S1.M1-01, M2.pin_2
  N7: S1.M1-02, M2.pin_1
  N8: S1.M2-01, M1.pin_2
  N9: S1.M2-02, M1.pin_1

custom parts:
  Adafruit T-Cobbler Plus: The Raspberry Pi has landed on the Maker World like a 40-GPIO pinned, quad-USB ported, credit card sized bomb of DIY joy. And while you can use most of our great Model B accessories by hooking up our downgrade cable, its probably a good time to upgrade your set up and accessorize using all of the 40 pins. That's why we now carry the Assembled Adafruit Pi T-Cobbler Plus - Breakout + Cable for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
  H-Bridge with L298N: h-bridge
