# Fritzing sketch x.Neopixels (saved by Fritzing 0.9.3b)
breadboards: 1

parts:
  Componente1 = 12 NeoPixel Ring [part_number=1643]
  Componente2 = Adafruit T-Cobbler Plus [part_number="Adafruit #1989 and #2028"]

nets:
  N1: Componente1.IN, Componente2.GPIO18
  VDD: Componente1.VDD, Componente2.+5V
  GND: Componente1.GND, Componente2.GND

custom parts:
  12 NeoPixel Ring: 12 ultra bright smart LED NeoPixels are arranged in a circle with 1.5" (37mm) outer diameter. The rings are 'chainable' - connect the output pin of one to the input pin of another. Use only one microcontroller pin to control as many as you can chain together! Each LED is addressable as the driver chip is inside the LED. Each one has ~18mA constant current drive so the color will be very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
  Adafruit T-Cobbler Plus: The Raspberry Pi has landed on the Maker World like a 40-GPIO pinned, quad-USB ported, credit card sized bomb of DIY joy. And while you can use most of our great Model B accessories by hooking up our downgrade cable, its probably a good time to upgrade your set up and accessorize using all of the 40 pins. That's why we now carry the Assembled Adafruit Pi T-Cobbler Plus - Breakout + Cable for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
